# Fritzing sketch pitot (saved by Fritzing 0.8.3b)
circuit board: 14.112cm x 2.22867cm
breadboards: 2

parts:
  U4 = ADR4533 [package=SOIC-8]
  R1 = Resistor [tolerance=±1% resistance=22 package="0805 [SMD]"]
  R2 = Resistor [tolerance=±1% resistance=22 package="0805 [SMD]"]
  R6 = Resistor [tolerance=±1% resistance=220 package="0805 [SMD]"]
  R5 = Resistor [tolerance=±1% resistance=220 package="0805 [SMD]"]
  U8 = LM334M [package=SO08]
  U7 = LM334M [package=SO08]
  U3 = LTC2493 [package=DFN-14]
  C3 = Tantalum Capacitor [capacitance=22µF voltage=10V package="B 3528 [SMD, tantalum]"]
  C4 = Ceramic Capacitor [capacitance=100nF voltage=10V package="0805 [SMD, multilayer]"]
  C5 = Ceramic Capacitor [capacitance=100nF voltage=10V package="0805 [SMD, multilayer]"]
  C1 = Tantalum Capacitor [capacitance=22µF voltage=10V package="B 3528 [SMD, tantalum]"]
  C2 = Ceramic Capacitor [capacitance=100nF voltage=10V package="0805 [SMD, multilayer]"]
  J2 = BeagleConn
  J1 = BattConn
  R9 = Resistor [tolerance=±5% resistance=22k package="0805 [SMD]"]
  R10 = Resistor [tolerance=±5% resistance=22k package="0805 [SMD]"]
  R13 = Resistor [tolerance=±5% resistance=22k package="0805 [SMD]"]
  R11 = Resistor [tolerance=±5% resistance=22k package="0805 [SMD]"]
  R12 = Resistor [tolerance=±5% resistance=22k package="0805 [SMD]"]
  U5 = SN74CB3Q3305 [package=TSSOP-8]
  U2 = AD7746 [package=tssop16]
  U9 = LM334M [package=SO08]
  U10 = LM334M [package=SO08]
  R4 = Resistor [tolerance=±1% resistance=22 package="0805 [SMD]"]
  R8 = Resistor [tolerance=±1% resistance=220 package="0805 [SMD]"]
  R7 = Resistor [tolerance=±1% resistance=220 package="0805 [SMD]"]
  R3 = Resistor [tolerance=±1% resistance=22 package="0805 [SMD]"]
  Pad2 = Pad [width=1.6 height=1.6 connect=center]  # not connected
  Pad3 = Pad [width=1.6 height=1.6 connect=center]  # not connected
  Pad4 = Pad [width=1.6 height=1.6 connect=center]  # not connected
  Pad6 = Pad [width=1.6 height=1.6 connect=center]  # not connected
  Pad7 = Pad [width=1.6 height=1.6 connect=center]  # not connected
  Pad8 = Pad [width=1.6 height=1.6 connect=center]  # not connected
  Pad9 = Pad [width=1.6 height=1.6 connect=center]  # not connected
  Pad10 = Pad [width=1.6 height=1.6 connect=center]  # not connected
  Pad11 = Pad [width=1.6 height=1.6 connect=center]  # not connected
  Pitot = Pitot [package=die]
  U6 = LM2937 [package=SOT-223]
  D1 = Rectifier Diode [part_number=1N4148 package=SOD-123]
  D2 = Rectifier Diode [part_number=1N4148 package=SOD-123]
  D3 = Rectifier Diode [part_number=1N4148 package=SOD-123]
  D4 = Rectifier Diode [part_number=1N4148 package=SOD-123]

nets (from the pcb view):
  VIN: U4.VIN, C4.1, C1.+, C2.1, J1.9V, U6.INPUT
  VCC: U4.VOUT, U3.VCC, U3.REF+, C5.1, U2.VDD
  N1: R1.Pin_0, R5.Pin_1, U7.R
  N2: R1.Pin_1, U7.V-, D1.anode
  N3: R2.Pin_0, R6.Pin_1, U8.R
  N4: R2.Pin_1, U8.V-, D2.anode
  N5: R6.Pin_0, Pitot.I2, D2.cathode
  N6: R5.Pin_0, Pitot.I3, D1.cathode
  N7: U8.V+, U7.V+, C3.+, R10.Pin_1, R11.Pin_1, U5.VCC, U9.V+, U10.V+, U6.OUTPUT
  GND: U3.f0, U3.GND, U3.COM, U3.REF-, C5.0, U2.GND, Pitot.GND
  N8: U3.SCL, R10.Pin_0, U5.1B, U2.SCL
  N9: U3.SDA, R11.Pin_0, U5.2B, U2.SDA
  N10: U3.CH0, Pitot.CH3
  N11: U3.CH1, Pitot.CH2
  N12: U3.CH2, Pitot.CH0
  N13: U3.CH3, Pitot.CH1
  N14: J2.3V3, R13.Pin_0, R12.Pin_0
  N15: J2.SCL, R13.Pin_1, U5.1A
  N16: J2.SDA, R12.Pin_1, U5.2A
  N17: J2.SEL, R9.Pin_0, U5.1OE, U5.2OE
  N18: U2.EXCA, Pitot.EXCA
  N19: U2.EXCB, Pitot.EXCB
  N20: U2.CIN1+, Pitot.CIN1+
  N21: U2.CIN2+, Pitot.CIN2+
  N22: U9.R, R7.Pin_1, R3.Pin_0
  N23: U9.V-, R3.Pin_1, D3.anode
  N24: U10.R, R4.Pin_0, R8.Pin_1
  N25: U10.V-, R4.Pin_1, D4.anode
  N26: R8.Pin_0, Pitot.I0, D4.cathode
  N27: R7.Pin_0, Pitot.I1, D3.cathode

custom parts:
  ADR4533: Ultralow noise, high accuracy voltage reference
  LM334M: 3-terminal adjustable current source
  LTC2493: 24-bit 2-/4-channel ΔΣ ADC with easy drive input current cancellation and I2C interface
  BeagleConn: Connector to Beaglebone black
  BattConn: Connector to 9V battery
  SN74CB3Q3305: Dual FET 2.5-V/3.3-V low-voltage high-bandwidth bus switch
  AD7746: 24-bit capacitance to digital converter
  Pitot: Pitot Chip
  LM2937: LM2937-3.3, 400mA voltage regulators
  Rectifier Diode: 1N4148 smd rectifier diode
